# Fritzing sketch sketch (saved by Fritzing 0.9.3b)

parts:
  NEOPIXEL1 = Neopixel Strip -- White (60/m) [part_number=1138]
  JACK1 = 2.1mm Barrel Jack with Terminal Block
  WeMos_D1_Mini1 = WeMos D1 Mini
  LED1 = Ruby the Red LED
  S1 = SWITCH-MOMENTARY-2 [package=tactile_switch_smd-2]

nets:
  N1: NEOPIXEL1.+5V#1, WeMos_D1_Mini1.5V
  N2: NEOPIXEL1.DI, WeMos_D1_Mini1.D5
  N3: NEOPIXEL1.GND#3, WeMos_D1_Mini1.G
  N4: NEOPIXEL1.GND#4, JACK1.NEG, LED1.anode, S1.1
  N5: NEOPIXEL1.+5V#6, JACK1.POS
  N6: WeMos_D1_Mini1.D3, S1.2
  N7: WeMos_D1_Mini1.D4, LED1.cathode

custom parts:
  Neopixel Strip -- White (60/m): Neopixel Strip, White, 60 pixels per meter.
