# Fritzing sketch sketch (saved by Fritzing 0.9.3b)

parts:
  NEOPIXEL1 = Neopixel Strip -- White (60/m) [part_number=1138]
  JACK1 = 2.1mm Barrel Jack with Terminal Block
  WeMos_D1_Mini1 = WeMos D1 Mini
  BUTTON1 = Arcade Button (red)  # not connected

nets:
  N1: NEOPIXEL1.+5V#1, WeMos_D1_Mini1.5V
  N2: NEOPIXEL1.DI, WeMos_D1_Mini1.D5
  N3: NEOPIXEL1.GND#3, WeMos_D1_Mini1.G
  N4: NEOPIXEL1.GND#4, JACK1.NEG
  N5: NEOPIXEL1.+5V#6, JACK1.POS

custom parts:
  Neopixel Strip -- White (60/m): Neopixel Strip, White, 60 pixels per meter.
  Arcade Button (red): Adafruit Arcade Button (red)
